# Fritzing sketch BarometerThermohygrometer_SwScience (saved by Fritzing 0.9.3b)
breadboards: 1

parts:
  パーツ1 = Arduino Nano (Rev3.0)
  Power_plug1 = Power plug
  R5 = Resistor [tolerance=±5% resistance=4.7k package=THT]
  R6 = Resistor [tolerance=±5% resistance=4.7k package=THT]

nets:
  GND: パーツ1.GND, Power_plug1.GND
  VIN: パーツ1.VIN, Power_plug1.VCC
  N1: パーツ1.A5, R6.Pin_1
  N2: パーツ1.A4, R5.Pin_1
  N3: パーツ1.3V3, R5.Pin_0, R6.Pin_0

notes:
  12V
  3.3V
  4.7kΩ
