# Fritzing sketch Camera2x2_SD (saved by Fritzing 0.9.4)
breadboards: 2

parts:
  パーツ1 = Arduino Nano (Rev3.0)
  IC3 = IC, DIP package, 18 pins [chip_label=IC]
  IC5 = IC, DIP package, 16 pins [chip_label=IC]
  Power_plug1 = Power plug
  IC6 = IC, DIP package, 16 pins [chip_label=IC]

nets:
  GND: パーツ1.GND, IC3.pin13, IC5.pin5, Power_plug1.GND, IC6.pin13
  N1: パーツ1.D7, IC5.pin1
  N2: パーツ1.D9, IC6.pin9
  N3: パーツ1.D10, IC3.pin17
  N4: パーツ1.D11/MOSI, IC3.pin16, IC5.pin2, IC6.pin10
  N5: パーツ1.D12/MISO, IC3.pin15, IC5.pin3, IC6.pin11
  VIN: パーツ1.VIN, Power_plug1.VCC
  N6: パーツ1.5V, IC3.pin10, IC5.pin6, IC6.pin14
  N7: パーツ1.A5, IC5.pin8, IC6.pin16
  N8: パーツ1.A4, IC5.pin7, IC6.pin15
  N9: パーツ1.D13/SCK, IC3.pin14, IC5.pin4, IC6.pin12

notes:
  5V
  SD
  Camera
  12V
