# Fritzing sketch Camera_SD (saved by Fritzing 0.9.3b)
breadboards: 1

parts:
  パーツ1 = Arduino Nano (Rev3.0)
  Power_plug1 = Power plug
  CAMERA1 = TTL Serial JPEG Camera
  R2 = Resistor [tolerance=±5% resistance=10k package=THT]
  R1 = Resistor [tolerance=±5% resistance=10k package=THT]
  IC3 = IC, DIP package, 18 pins [chip_label=IC]

nets:
  GND: パーツ1.GND, Power_plug1.GND, CAMERA1.GND, R1.Pin_1, IC3.pin13
  N1: パーツ1.D2, CAMERA1.TX
  N2: パーツ1.D3, R2.Pin_0
  N3: パーツ1.D10, IC3.pin17
  N4: パーツ1.D11/MOSI, IC3.pin16
  N5: パーツ1.D12/MISO, IC3.pin15
  VIN: パーツ1.VIN, Power_plug1.VCC
  5V: パーツ1.5V, CAMERA1.5V, IC3.pin10
  N6: パーツ1.D13/SCK, IC3.pin14
  N7: CAMERA1.RX, R2.Pin_1, R1.Pin_0

notes:
  10kΩ
  12V
  5V

custom parts:
  TTL Serial JPEG Camera: TTL Serial JPEG Camera with NTSC Out
