# Fritzing sketch DCMotor (saved by Fritzing 0.9.3b)
breadboards: 1

parts:
  パーツ1 = Arduino Nano (Rev3.0)
  Power_plug1 = Power plug
  C2 = Ceramic Capacitor [capacitance=100nF package="100 mil [THT, multilayer]"]
  C3 = Electrolytic Capacitor [capacitance=1µF package="100 mil [THT, electrolytic]"]
  C4 = Ceramic Capacitor [capacitance=100nF package="100 mil [THT, multilayer]"]
  VCC1 = Battery
  M1 = DC Motor
  C9 = Electrolytic Capacitor [capacitance=1µF package="100 mil [THT, electrolytic]"]
  C10 = Ceramic Capacitor [capacitance=100nF package="100 mil [THT, multilayer]"]

nets:
  GND: パーツ1.GND, Power_plug1.GND, C2.0, C3.-, VCC1.-, C9.-, C10.0
  VIN: パーツ1.VIN, Power_plug1.VCC
  N1: パーツ1.5V, C9.+, C10.1
  N2: C2.1, C3.+, VCC1.+
  N3: C4.0, M1.pin_2
  N4: C4.1, M1.pin_1

notes:
  12V
  5V
  100uF
  0.1uF
  MotorDriver
  Battery for DC motor
  DC Motor
  1uF
