# Fritzing sketch IMU_Pololu (saved by Fritzing 0.9.3b)
breadboards: 1

parts:
  パーツ1 = Arduino Nano (Rev3.0)
  Power_plug1 = Power plug

nets:
  GND: パーツ1.GND, Power_plug1.GND
  VIN: パーツ1.VIN, Power_plug1.VCC

notes:
  5V
  12V
  VIN
  SCL
  SDA
  GND
  VDD
