# Fritzing sketch Light (saved by Fritzing 0.9.3b)
breadboards: 1

parts:
  パーツ1 = Arduino Nano (Rev3.0)
  Power_plug1 = Power plug
  R1 = Photocell (LDR) [package=THT]
  R2 = Resistor [tolerance=±5% resistance=1k package=THT]

nets:
  GND: パーツ1.GND, Power_plug1.GND, R2.Pin_1
  VIN: パーツ1.VIN, Power_plug1.VCC
  N1: パーツ1.5V, R1.pin_0
  N2: パーツ1.A0, R1.pin_1, R2.Pin_0

notes:
  1kΩ
  12V
  5V
