# Fritzing sketch SD (saved by Fritzing 0.9.3b)
breadboards: 1

parts:
  パーツ1 = Arduino Nano (Rev3.0)
  Power_plug1 = Power plug
  IC2 = IC, DIP package, 18 pins [chip_label=IC]

nets:
  GND: パーツ1.GND, Power_plug1.GND, IC2.pin13
  N1: パーツ1.D10, IC2.pin17
  N2: パーツ1.D11/MOSI, IC2.pin16
  N3: パーツ1.D12/MISO, IC2.pin15
  VIN: パーツ1.VIN, Power_plug1.VCC
  N4: パーツ1.5V, IC2.pin10
  N5: パーツ1.D13/SCK, IC2.pin14

notes:
  12V
  5V
