# Fritzing sketch Servo (saved by Fritzing 0.9.3b)
breadboards: 1

parts:
  パーツ1 = Arduino Nano (Rev3.0)
  Power_plug1 = Power plug
  J1 = Basic Servo

nets:
  GND: パーツ1.GND, Power_plug1.GND, J1.gnd
  N1: パーツ1.D4, J1.pulse
  VIN: パーツ1.VIN, Power_plug1.VCC
  5V: パーツ1.5V, J1.vcc

notes:
  12V
  5V
