# Fritzing sketch XBee (saved by Fritzing 0.9.3b)
breadboards: 1

parts:
  パーツ1 = Arduino Nano (Rev3.0)
  Power_plug1 = Power plug
  パーツ2 = XBee Explorer Regulated
  U1 = XBEE-1 [package=xbee-silk]  # not connected

nets:
  GND: パーツ1.GND, Power_plug1.GND, パーツ2.GND
  N1: パーツ1.D2, パーツ2.DOUT
  N2: パーツ1.D3, パーツ2.DIN
  VIN: パーツ1.VIN, Power_plug1.VCC
  5V: パーツ1.5V, パーツ2.5V

notes:
  12V
  5V
  ↓
